// Logisim project Harware Implementation.circ as structural Verilog: 5 circuits, main circuit main
module main (
  input  _1,
  input  _1_2,
  input  _1_3,
  input  in_4,
  input  in_5,
  input  _1_4,
  input  _1_5,
  input  in_8,
  output out_9,
  output Units_consumed,
  output out_11,
  output out_12,
  output out_13,
  output out_14,
  output out_15,
  output out_16,
  output out_17,
  output ALERT
);

  wire and_1_out, and_2_out, clock_1_out, not_1_out, not_2_out, not_3_out, not_4_out, not_5_out, not_6_out,
       or_1_out;

  Clock clock_1 (.out(clock_1_out));
  _2bit_counter u_2bit_counter_1 (.out_3(Units_consumed), .out_2(out_9), .in_1(clock_1_out));
  not not_1 (not_1_out, out_9);
  or or_1 (or_1_out, not_1_out, Units_consumed);
  _2_bit_Adder_Subtractor u_2_bit_adder_subtractor_1 (
    .Cin(_1_3), .A_lsb(or_1_out), .A_msb(out_9), .B_lsb(in_8), .B_msb(_1_5), .S0(out_12), .S1(out_11));
  or or_2 (out_14, out_11, out_12);
  not not_2 (not_2_out, out_11);
  not not_3 (not_3_out, out_14);
  _3bit_Adder_Subtractor u_3bit_adder_subtractor_1 (
    .Cin(_1), .A_lsb(in_5), .B_lsb(not_3_out), .B_msb(_1_4), .in_6(not_2_out), .A_msb(_1_2), .in_3(in_4),
    .out_8(out_17), .out_9(out_16), .out_10(out_15));
  not not_4 (not_4_out, out_15);
  not not_5 (not_5_out, out_17);
  not not_6 (not_6_out, out_16);
  and and_1 (and_1_out, not_4_out, not_5_out);
  and and_2 (and_2_out, not_6_out, out_17);
  or or_3 (ALERT, and_1_out, and_2_out);

  assign out_13 = out_11;

  // Notes on the sheet:
  //   free limit = 1
  //   price consumed
  //   prepaid amount
  //   BALANCE MONEY
endmodule

module Full_Adder (
  input  Cin,
  input  A,
  input  in_3,
  output S,
  output Cout
);

  wire and_1_out, and_2_out, xor_1_out;

  xor xor_1 (xor_1_out, A, in_3);
  and and_1 (and_1_out, A, in_3);
  xor xor_2 (S, Cin, xor_1_out);
  and and_2 (and_2_out, Cin, xor_1_out);
  or or_1 (Cout, and_1_out, and_2_out);
endmodule

// Freelimit Subtractor
module _2_bit_Adder_Subtractor (
  input  Cin,
  input  A_msb,
  input  A_lsb,
  input  B_lsb,
  input  B_msb,
  output S1,
  output S0
);

  wire full_adder_1_cout;

  Full_Adder full_adder_1 (.Cin(Cin), .A(A_lsb), .S(S0), .Cout(full_adder_1_cout), .in_3(B_lsb));
  Full_Adder full_adder_2 (.Cin(full_adder_1_cout), .A(A_msb), .S(S1), .in_3(B_msb));  // open: Cout
endmodule

// Electricity Units Counter
module _2bit_counter (
  input  in_1,
  output out_2,
  output out_3
);

  wire d_ff_1_qn, d_ff_2_qn;

  D_Flip_Flop d_ff_1 (.clk(in_1), .D(d_ff_1_qn), .Q(out_3), .Qn(d_ff_1_qn));  // open: preset, en, reset
  D_Flip_Flop d_ff_2 (.clk(d_ff_1_qn), .D(d_ff_2_qn), .Q(out_2), .Qn(d_ff_2_qn));  // open: preset, en, reset
endmodule

// Balance Generator
module _3bit_Adder_Subtractor (
  input  Cin,
  input  A_msb,
  input  in_3,
  input  A_lsb,
  input  B_lsb,
  input  in_6,
  input  B_msb,
  output out_8,
  output out_9,
  output out_10
);

  wire full_adder_1_cout, full_adder_2_cout;

  Full_Adder full_adder_1 (.Cin(Cin), .A(A_lsb), .S(out_8), .Cout(full_adder_1_cout), .in_3(B_lsb));
  Full_Adder full_adder_2 (.Cin(full_adder_1_cout), .A(in_3), .S(out_9), .Cout(full_adder_2_cout), .in_3(in_6));
  Full_Adder full_adder_3 (.Cin(full_adder_2_cout), .A(A_msb), .S(out_10), .in_3(B_msb));  // open: Cout
endmodule
