// Logisim project S1-T17.circ as structural Verilog: 6 circuits, main circuit main
module main (
  input  [9:0] A,
  input  [9:0] danger_level___45_rs,
  input  [9:0] free_limit___50_units,
  input  [9:0] higher_limit_of_range_1___50,
  input  [9:0] lower_limit_of_range_1___1,
  input  [9:0] higher_limit_of_raange_2___150,
  input  [9:0] price_per_unit_in_range_2___2rs,
  input  [9:0] price_per_unit_in_range_3___3rs,
  input  [9:0] B,
  input  _1_X,
  input  _1_Y,
  input  _0___Z,
  input  [9:0] prepaid_money,
  output [9:0] total_units_consumed,
  output [9:0] balance_money,
  output [9:0] average_consumption_per_day_in_terms_of_money,
  output [9:0] with_the_current_usage_pattern_how_much_more_days_will_the_plan_last
);

  wire comparator_1_eq, comparator_2_gt, comparator_3_eq, comparator_4_eq, comparator_4_lt, DATE_TRIGGER_out,
       or_1_out, range1_units_consumed_1_input_for_next_range, range2_units_consumed_1_input_for_next_range,
       SENSOR_INPUT_out;
  wire [9:0] adder_1_out, adder_2_out, date_counter_1_out_5, date_counter_1_out_6, multiplier_1_out,
       multiplier_2_out, range1_units_consumed_1_units_to_be_multiplied_in_range_1,
       range2_units_consumed_1_units_to_be_multiplied_in_range_2,
       range3_units_consumed_1_units_to_be_multiplied_in_range_3, register_1_q, subtractor_free_limit_1_out_4;

  Clock SENSOR_INPUT (.out(SENSOR_INPUT_out));
  Clock DATE_TRIGGER (.out(DATE_TRIGGER_out));
  Comparator #(.width(10)) comparator_1 (.a(date_counter_1_out_6), .b(A), .eq(comparator_1_eq));  // open: gt, lt
  Date_Counter date_counter_1 (
    .Date_Trigger(DATE_TRIGGER_out), .out_6(date_counter_1_out_6), .in_1(_1_Y), .in_2(_0___Z), .in_4(A),
    .out_5(date_counter_1_out_5));
  Counter #(.width(10), .max('h3ff)) counter_1 (
    .count(_1_X), .Q(total_units_consumed), .clk(SENSOR_INPUT_out), .clr(comparator_1_eq));  // open: load, D, carry
  Comparator #(.width(10)) comparator_2 (
    .a(total_units_consumed), .b(free_limit___50_units), .gt(comparator_2_gt));  // open: eq, lt
  SUBTRACTOR_free_limit subtractor_free_limit_1 (
    .free_limit_50_units(free_limit___50_units), .units_consumed_from_counter(total_units_consumed),
    .comparator_s_output(comparator_2_gt), .out_4(subtractor_free_limit_1_out_4));
  range1_units_consumed range1_units_consumed_1 (
    ._0_for_else_condition(B), .units_consumed_after_free_limit(subtractor_free_limit_1_out_4),
    .lower_limit_of_range_1_1(lower_limit_of_range_1___1),
    .higher_limit_of_range_1__50(higher_limit_of_range_1___50),
    .input_for_next_range(range1_units_consumed_1_input_for_next_range),
    .units_to_be_multiplied_in_range_1(range1_units_consumed_1_units_to_be_multiplied_in_range_1));
  range2_units_consumed range2_units_consumed_1 (
    ._0_for_else_condition(B), .units_consumed_after_free_limit(subtractor_free_limit_1_out_4),
    .higher_limit_of_range_2_150(higher_limit_of_raange_2___150),
    .input_from_previous_range(range1_units_consumed_1_input_for_next_range),
    .input_for_next_range(range2_units_consumed_1_input_for_next_range),
    .higher_limit_of_previous_range_for_subtraction_50(higher_limit_of_range_1___50),
    .units_to_be_multiplied_in_range_2(range2_units_consumed_1_units_to_be_multiplied_in_range_2));
  range3_units_consumed range3_units_consumed_1 (
    .units_consumed_after_free_limit(subtractor_free_limit_1_out_4),
    .higher_limit_of_previous_range_for_subtraction(higher_limit_of_raange_2___150),
    .input_from_previous_range(range2_units_consumed_1_input_for_next_range),
    .if_units_consumed_is_less_than_range_3(B),
    .units_to_be_multiplied_in_range_3(range3_units_consumed_1_units_to_be_multiplied_in_range_3));
  Multiplier #(.width(10)) multiplier_1 (
    .a(price_per_unit_in_range_2___2rs), .b(range2_units_consumed_1_units_to_be_multiplied_in_range_2),
    .out(multiplier_1_out));  // open: cin, cout
  Multiplier #(.width(10)) multiplier_2 (
    .a(price_per_unit_in_range_3___3rs), .b(range3_units_consumed_1_units_to_be_multiplied_in_range_3),
    .out(multiplier_2_out));  // open: cin, cout
  Adder #(.width(10)) adder_1 (.a(multiplier_1_out), .b(multiplier_2_out), .out(adder_1_out));  // open: cin, cout
  Adder #(.width(10)) adder_2 (
    .a(range1_units_consumed_1_units_to_be_multiplied_in_range_1), .b(adder_1_out), .out(adder_2_out));  // open: cin, cout
  Subtractor #(.width(10)) subtractor_1 (.a(prepaid_money), .b(adder_2_out), .out(balance_money));  // open: bin, bout
  Register #(.width(10)) register_1 (
    .D(adder_2_out), .en(DATE_TRIGGER_out), .Q(register_1_q), .clk(DATE_TRIGGER_out));  // open: clr
  Divider #(.width(10)) divider_1 (
    .a(register_1_q), .b(date_counter_1_out_5), .out(average_consumption_per_day_in_terms_of_money));  // open: upper, rem
  Comparator #(.width(10)) comparator_3 (.a(balance_money), .b(B), .eq(comparator_3_eq));  // open: gt, lt
  Comparator #(.width(10)) comparator_4 (
    .a(balance_money), .b(danger_level___45_rs), .eq(comparator_4_eq), .lt(comparator_4_lt));  // open: gt
  Divider #(.width(10)) divider_2 (
    .a(balance_money), .b(average_consumption_per_day_in_terms_of_money),
    .out(with_the_current_usage_pattern_how_much_more_days_will_the_plan_last));  // open: upper, rem
  or or_1 (or_1_out, comparator_4_eq, comparator_4_lt);
  LED ALERT1_when_balance_is_0 (.in(comparator_3_eq));
  LED ALERT2_when_balance_is_less (.in(or_1_out));

  // Notes on the sheet:
  //   gives units consumed after free limit
  //   price per unit in range 1 = 1rs
  //   How to use:
  //   3. Set 'free limit' to 0000110010(50 units)
  //   9. Set the following-
  //   A - 0000000000
  //   B - 0000000001
  //   10. Set the following switches as follows - 
  //   X - 1
  //   Y - 1
  //   Z - 0
  //   (2 presses = 1 unit of electricity consumed)
  //   1. Set 'prepaid money' (in rs) as you wish
  //   2. Set 'danger level' to 0000101101 (45 rs)
  //   4. Set 'higher limit of range 1' to 0000110010 ( 50 units)
  //   5. Set 'lower limit of range 1' to 0000000001(1 unit)
  //   6. Set 'higher limit of range 2 to '0010010110(150 units)
  //   7. Set 'price per unit in range 2' to 0000000010 ( 2 rupees)
  //   8. Set 'price per unit in range 3' to 0000000011 (3 rupees)
  //   First press 'DATE TRIGGER' to increase date from 1 to 31.
  //   You will get outputs in the top right corner of circuit
  //   when balance money becomes 0 (shown by alert1)
  //   You can set your prepaid amount to next credit you want to purchase
  //   Press the 'SENSOR INPUT' twice to increase electricity units consumed by 1
  //   PREPAID ENERGY MANAGEMENT SYSTEM
  //   TEAM DETAILS: 
  //   Charuneya M, 231CS117
  //   Dhiya N, 231CS121
  //   Neha Chandrashekar, 231CS137
endmodule

// SUBTRACTOR
module SUBTRACTOR_free_limit (
  input  [9:0] free_limit_50_units,
  input  [9:0] units_consumed_from_counter,
  input  comparator_s_output,
  output [9:0] out_4
);

  wire [9:0] multiplexer_1_out;

  Multiplexer #(.width(10), .enable("false")) multiplexer_1 (
    .in0(free_limit_50_units), .in1(units_consumed_from_counter), .out(multiplexer_1_out),
    .sel(comparator_s_output));
  Subtractor #(.width(10)) subtractor_1 (
    .a(multiplexer_1_out), .b(free_limit_50_units), .out(out_4));  // open: bin, bout
endmodule

// RANGE 1
module range1_units_consumed (
  input  [9:0] _0_for_else_condition,
  input  [9:0] units_consumed_after_free_limit,
  input  [9:0] lower_limit_of_range_1_1,
  input  [9:0] higher_limit_of_range_1__50,
  output [9:0] units_to_be_multiplied_in_range_1,
  output input_for_next_range
);

  wire and_1_out, comparator_1_eq, comparator_1_gt, comparator_2_eq, comparator_2_lt, or_1_out, or_2_out;
  wire [9:0] multiplexer_1_out;

  Comparator #(.width(10)) comparator_1 (
    .a(units_consumed_after_free_limit), .b(lower_limit_of_range_1_1), .gt(comparator_1_gt),
    .eq(comparator_1_eq));  // open: lt
  Comparator #(.width(10)) comparator_2 (
    .a(units_consumed_after_free_limit), .b(higher_limit_of_range_1__50), .gt(input_for_next_range),
    .eq(comparator_2_eq), .lt(comparator_2_lt));
  or or_1 (or_1_out, comparator_1_gt, comparator_1_eq);
  or or_2 (or_2_out, comparator_2_eq, comparator_2_lt);
  and and_1 (and_1_out, or_1_out, or_2_out);
  Multiplexer #(.width(10), .enable("false")) multiplexer_1 (
    .in0(_0_for_else_condition), .in1(units_consumed_after_free_limit), .out(multiplexer_1_out),
    .sel(and_1_out));
  Multiplexer #(.width(10), .enable("false")) multiplexer_2 (
    .in0(multiplexer_1_out), .in1(higher_limit_of_range_1__50), .out(units_to_be_multiplied_in_range_1),
    .sel(input_for_next_range));
endmodule

// RANGE 2
module range2_units_consumed (
  input  [9:0] _0_for_else_condition,
  input  [9:0] units_consumed_after_free_limit,
  input  [9:0] higher_limit_of_range_2_150,
  input  [9:0] higher_limit_of_previous_range_for_subtraction_50,
  input  input_from_previous_range,
  output [9:0] units_to_be_multiplied_in_range_2,
  output input_for_next_range
);

  wire comparator_1_eq, comparator_1_lt, or_1_out, subtractor_1_bout;
  wire [9:0] multiplexer_1_out, multiplexer_2_out, subtractor_1_out;

  Multiplexer #(.width(10), .enable("false")) multiplexer_1 (
    .in0(_0_for_else_condition), .in1(units_consumed_after_free_limit), .out(multiplexer_1_out),
    .sel(input_from_previous_range));
  Comparator #(.width(10)) comparator_1 (
    .a(multiplexer_1_out), .b(higher_limit_of_range_2_150), .gt(input_for_next_range), .eq(comparator_1_eq),
    .lt(comparator_1_lt));
  or or_1 (or_1_out, comparator_1_eq, comparator_1_lt);
  Multiplexer #(.width(10), .enable("false")) multiplexer_2 (
    .in0(higher_limit_of_range_2_150), .in1(units_consumed_after_free_limit), .out(multiplexer_2_out),
    .sel(or_1_out));
  Subtractor #(.width(10)) subtractor_1 (
    .a(multiplexer_2_out), .b(higher_limit_of_previous_range_for_subtraction_50), .out(subtractor_1_out),
    .bout(subtractor_1_bout));  // open: bin
  Multiplexer #(.width(10), .enable("false")) multiplexer_3 (
    .in0(subtractor_1_out), .in1(_0_for_else_condition), .out(units_to_be_multiplied_in_range_2),
    .sel(subtractor_1_bout));
endmodule

// RANGE 3
module range3_units_consumed (
  input  [9:0] units_consumed_after_free_limit,
  input  [9:0] higher_limit_of_previous_range_for_subtraction,
  input  input_from_previous_range,
  input  [9:0] if_units_consumed_is_less_than_range_3,
  output [9:0] units_to_be_multiplied_in_range_3
);

  wire subtractor_1_bout;
  wire [9:0] multiplexer_1_out, subtractor_1_out;

  Multiplexer #(.width(10), .enable("false")) multiplexer_1 (
    .in0(higher_limit_of_previous_range_for_subtraction), .in1(units_consumed_after_free_limit),
    .out(multiplexer_1_out), .sel(input_from_previous_range));
  Subtractor #(.width(10)) subtractor_1 (
    .a(multiplexer_1_out), .b(higher_limit_of_previous_range_for_subtraction), .out(subtractor_1_out),
    .bout(subtractor_1_bout));  // open: bin
  Multiplexer #(.width(10), .enable("false")) multiplexer_2 (
    .in0(subtractor_1_out), .in1(if_units_consumed_is_less_than_range_3),
    .out(units_to_be_multiplied_in_range_3), .sel(subtractor_1_bout));
endmodule

// DATE COUNTER
module Date_Counter (
  input  in_1,
  input  in_2,
  input  Date_Trigger,
  input  [9:0] in_4,
  output [9:0] out_5,
  output [9:0] out_6
);

  Counter #(.width(10), .max('h1e)) counter_1 (
    .count(in_1), .Q(out_5), .clk(Date_Trigger), .clr(in_2));  // open: load, D, carry
  Adder #(.width(10)) adder_1 (.a(out_5), .b(in_4), .out(out_6));  // open: cin, cout
endmodule
